# Fritzing sketch Aquamino (saved by Fritzing 0.9.0b)
circuit board: 8.46667cm x 5.64444cm
stripboards: 1

parts:
  Part1 = Arduino Leonardo (Rev3b)
  Part2 = Real Time Clock Module - DS1307 RTC Breakout Board
  DS1 = DS18B20 1-Wire Temperature Sensor [part_number=DS18B20]
  R1 = Resistor [tolerance=±5% resistance=4.7k package=THT]
  T1 = LM35 Temperature Sensor [package="TO92 [THT]"]
  C1 = Ceramic Capacitor [capacitance=1µF package="100 mil [THT, multilayer]"]
  R2 = Resistor [tolerance=±5% resistance=68 package=THT]

nets:
  5V: Part1.5V, Part2.5V, DS1.VDD, R1.Pin_1, T1.+Vs
  GND: Part1.GND, Part2.GND, DS1.GND, T1.GND, R2.Pin_0
  N1: Part1.D8/A8, DS1.DQ, R1.Pin_0
  N2: Part1.SDA, Part2.SCL
  N3: Part1.SCL, Part2.SDA
  N4: T1.Vout, C1.0
  N5: C1.1, R2.Pin_1
